// Logisim project uP.circ as structural Verilog: 6 circuits, main circuit main
module main (
);

  wire [3:0] Opcode;
  wire [7:0] X, Y;

  DipSwitch dipswitch_1 (
    .sw1(X[7]), .sw2(X[6]), .sw3(X[5]), .sw4(X[4]), .sw5(X[3]), .sw6(X[2]), .sw7(X[1]), .sw8(X[0]));
  DipSwitch dipswitch_2 (
    .sw1(Y[7]), .sw2(Y[6]), .sw3(Y[5]), .sw4(Y[4]), .sw5(Y[3]), .sw6(Y[2]), .sw7(Y[1]), .sw8(Y[0]));
  DipSwitch #(.number(4)) dipswitch_3 (.sw1(Opcode[3]), .sw2(Opcode[2]), .sw3(Opcode[1]), .sw4(Opcode[0]));
endmodule

module Adder8bits (
  input  Cin,
  input  [7:0] Y,
  input  [7:0] X,
  output [7:0] Result,
  output Overflow
);

  wire adder_1_cout, adder_2_cout, adder_3_cout, adder_4_cout, adder_5_cout, adder_6_cout, adder_7_cout;

  Adder #(.width(1)) adder_1 (.a(Y[0]), .b(X[0]), .out(Result[0]), .cin(Cin), .cout(adder_1_cout));
  Adder #(.width(1)) adder_2 (.a(Y[1]), .b(X[1]), .out(Result[1]), .cin(adder_1_cout), .cout(adder_2_cout));
  Adder #(.width(1)) adder_3 (.a(Y[2]), .b(X[2]), .out(Result[2]), .cin(adder_2_cout), .cout(adder_3_cout));
  Adder #(.width(1)) adder_4 (.a(Y[3]), .b(X[3]), .out(Result[3]), .cin(adder_3_cout), .cout(adder_4_cout));
  Adder #(.width(1)) adder_5 (.a(Y[4]), .b(X[4]), .out(Result[4]), .cin(adder_4_cout), .cout(adder_5_cout));
  Adder #(.width(1)) adder_6 (.a(Y[5]), .b(X[5]), .out(Result[5]), .cin(adder_5_cout), .cout(adder_6_cout));
  Adder #(.width(1)) adder_7 (.a(Y[6]), .b(X[6]), .out(Result[6]), .cin(adder_6_cout), .cout(adder_7_cout));
  Adder #(.width(1)) adder_8 (.a(Y[7]), .b(X[7]), .out(Result[7]), .cin(adder_7_cout), .cout(Overflow));
endmodule

module Substractor8bits (
  input  Cin,
  input  [7:0] X,
  input  [7:0] Y,
  output [7:0] Result,
  output Underflow
);

  wire subtractor_1_bout, subtractor_2_bout, subtractor_3_bout, subtractor_4_bout, subtractor_5_bout,
       subtractor_6_bout, subtractor_7_bout;

  Subtractor #(.width(1)) subtractor_1 (.a(X[0]), .b(Y[0]), .out(Result[0]), .bin(Cin), .bout(subtractor_1_bout));
  Subtractor #(.width(1)) subtractor_2 (
    .a(X[1]), .b(Y[1]), .out(Result[1]), .bin(subtractor_1_bout), .bout(subtractor_2_bout));
  Subtractor #(.width(1)) subtractor_3 (
    .a(X[2]), .b(Y[2]), .out(Result[2]), .bin(subtractor_2_bout), .bout(subtractor_3_bout));
  Subtractor #(.width(1)) subtractor_4 (
    .a(X[3]), .b(Y[3]), .out(Result[3]), .bin(subtractor_3_bout), .bout(subtractor_4_bout));
  Subtractor #(.width(1)) subtractor_5 (
    .a(X[4]), .b(Y[4]), .out(Result[4]), .bin(subtractor_4_bout), .bout(subtractor_5_bout));
  Subtractor #(.width(1)) subtractor_6 (
    .a(X[5]), .b(Y[5]), .out(Result[5]), .bin(subtractor_5_bout), .bout(subtractor_6_bout));
  Subtractor #(.width(1)) subtractor_7 (
    .a(X[6]), .b(Y[6]), .out(Result[6]), .bin(subtractor_6_bout), .bout(subtractor_7_bout));
  Subtractor #(.width(1)) subtractor_8 (.a(X[7]), .b(Y[7]), .out(Result[7]), .bin(subtractor_7_bout), .bout(Underflow));
endmodule

module And8bits (
  input  [7:0] X,
  input  [7:0] Y,
  output [7:0] Result
);

  assign Result = X & Y;  // AND_Gate and_1, 8 bits wide
endmodule

module Or8bits (
  input  [7:0] X,
  input  [7:0] Y,
  output [7:0] Result
);

  assign Result = X | Y;  // OR_Gate or_1, 8 bits wide
endmodule

module Not8bits (
  input  [7:0] X,
  output [7:0] Result
);

  assign Result = ~X;  // NOT_Gate not_1, 8 bits wide
endmodule
